# Fritzing sketch p2gstick (saved by Fritzing 0.8.3b)
circuit board: 5.5cm x 3cm
breadboards: 1

parts:
  MT29F1G08ABADAWP_D1 = MT29F1G08ABADAWP:D [part_number=MT29F1G08ABADAWP:D package=tsop48]  # not connected
  IC1 = AT32UC3A3256S-ALUT [package=LQFP-144]
  USBCONN = USB Connectors [package=usb-a-h]
  C3 = Ceramic Capacitor [capacitance=47µF package="0603 [SMD, multilayer]"]
  C4 = Ceramic Capacitor [capacitance=47µF package="0603 [SMD, multilayer]"]
  C5 = Ceramic Capacitor [capacitance=47µF package="0603 [SMD, multilayer]"]
  C6 = Ceramic Capacitor [capacitance=47µF package="0603 [SMD, multilayer]"]
  C7 = Ceramic Capacitor [capacitance=47µF package="0603 [SMD, multilayer]"]
  IC2 = TLV1117-33 [part_number=595-TLV1117-33IDCY package=sot223]
  U1 = TPD2S017DBVR [part_number=595-TPD2S017DBVR package=SOT23-6]
  R1 = Resistor [tolerance=±5% resistance=22 package="0805 [SMD]"]  # not connected

nets:
  N1: IC1.6, U1.Ch1_Out
  N2: USBCONN.D-, U1.Ch2_In
  N3: USBCONN.D+, U1.Ch1_In
  N4: USBCONN.VBUS, IC2.IN
  GND: USBCONN.GND, C3.1, C4.1, C5.1, C6.1, C7.1, IC2.GND
  3.3V: C3.0, C4.0, C5.0, C6.0, C7.0, IC2.OUT

custom parts:
  MT29F1G08ABADAWP:D: Mircon MT29F1G08ABADAWP:D NAND flash
  AT32UC3A3256S-ALUT: IC1
  TLV1117-33: The TLV1117 is a positive low-dropout voltage regulator designed to provide up to 800 mA of output current. The device is available in 1.5-V, 1.8-V, 2.5-V, 3.3-V, 5-V, and adjustable-output voltage options. All internal circuitry is designed to operate down to 1-V input-to-output differential. Dropout voltage is specified at a maximum of 1.3 V at 800 mA, decreasing at lower load currents.
  TPD2S017DBVR: The TPD2S017 provides a robust system-level ESD solution for the high-speed lines interfacing low-voltage, ESD-sensitive core chipset. This device offers two stage ESD clamps in each line with ≈1-Ω series resistor isolation. This architecture allows the device to generate very low clamp voltage during system level ESD strikes. Due to the series resistor component, the TPD2S017 provides a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
